# Fritzing sketch scheme (saved by Fritzing 0.9.3b)

parts:
  Часть1 = Arduino Nano (Rev3.0)
  GSM_SIM_GPSR_SMS_SIM900_SIM1 = SIM800L [package=THT]
  LED1 = smd LED [color="Red (633nm)" package="0603 [SMD]"]
  Keypad4x1 = Keypad Membran 4x4  # not connected
  Часть2 = LCD1602-I2C
  R1 = Resistor [tolerance=±5% resistance=10 package=THT]
  R2 = Resistor [tolerance=±5% resistance=10 package=THT]
  VCC1 = Battery
  S2 = Pushbutton [package=THT]
  S3 = Pushbutton [package=THT]  # not connected
  S4 = Pushbutton [package=THT]
  U1 = MIC [package=mic_electret_smd]  # not connected

nets:
  GND: Часть1.GND, Часть2.GND, R2.Pin_0
  5V: Часть1.5V, Часть2.VCC, S4.leg1
  N1: Часть1.A5, Часть2.SCL
  N2: Часть1.A4, Часть2.SDA
  N3: Часть1.A1, GSM_SIM_GPSR_SMS_SIM900_SIM1.SIM_TXD
  N4: Часть1.A0, R1.Pin_0
  N5: GSM_SIM_GPSR_SMS_SIM900_SIM1.SIM_RXD, R1.Pin_1
  N6: GSM_SIM_GPSR_SMS_SIM900_SIM1.GND, LED1.cathode, VCC1.-
  N7: LED1.anode, S2.leg0
  N8: VCC1.+, S2.leg1, S4.leg0

custom parts:
  Keypad Membran 4x4: Membrane Keypad 4x4 Matrix
  LCD1602-I2C: A standard character display, usually with 2x16 characters. Comes in many colors with LCM1602 IIC attached.
